# Fritzing sketch OpenMacroRail (saved by Fritzing 0.8.7b)
circuit board: 5.27101cm x 5.32643cm
breadboards: 1

parts:
  IC1 = ULN2803A [package=THT]
  TRS1 = Audio Jack (TRS) 3.5mm [package="PG203J [THT]"]
  J1 = male pin header, 5 pins [form="♂ (male)"]
  IC2 = CNY 74-2 [package=dip08]
  Shield = Arduino Uno (Rev3)

nets (from the pcb view):
  N1: IC1.In_1, IC1.In_2, Shield.D5_PWM
  N2: IC1.In_3, IC1.In_4, Shield.D4
  N3: IC1.In_5, IC1.In_6, Shield.D3_PWM
  N4: IC1.In_7, IC1.In_8, Shield.D2
  N5: IC1.0V, IC2.D1-C, IC2.D2-C, Shield.GND
  N6: IC1.COM_-_Common, J1.pin1, Shield.5V
  N7: IC1.Out_8, IC1.Out_7, J1.pin2
  N8: IC1.Out_6, IC1.Out_5, J1.pin3
  N9: IC1.Out_4, IC1.Out_3, J1.pin4
  N10: IC1.Out_2, IC1.Out_1, J1.pin5
  N11: TRS1.Sleeve, IC2.T2-C
  N12: TRS1.Tip, IC2.T2-E, IC2.T1-C, IC2.T1-E
  N13: IC2.D1-A, Shield.D13/SCK
  N14: IC2.D2-A, Shield.D12/MISO

notes:
  OpenMacroRail

custom parts:
  CNY 74-2: CNY 74-2 Dual Opto Coupler
